# Fritzing sketch AR10_Remote safe (saved by Fritzing 0.9.3b)
breadboards: 1

parts:
  부품1 = Arduino Uno (Rev3)
  LED1 = LED - 5mm [color="Red (633nm)" package="5 mm [THT]"]
  LED2 = LED - 5mm [color="Green (570nm)" package="5 mm [THT]"]
  R1 = Resistor [tolerance=±5% resistance=220 package=THT]
  R2 = Resistor [tolerance=±5% resistance=220 package=THT]
  J1 = Basic Servo
  Q1 = PNP-Transistor [package="TO92 [THT]"]
  LCD1 = LCD screen

nets:
  N1: 부품1.A0, Q1.C
  N2: 부품1.A4/SDA, LCD1.RS
  N3: 부품1.A5/SCL, LCD1.V0
  N4: 부품1.D8, R2.Pin_1
  N5: 부품1.D9_PWM, J1.pulse
  N6: 부품1.D10_PWM/SS, R1.Pin_1
  5V: 부품1.5V, J1.vcc, Q1.B, LCD1.VDD
  GND: 부품1.GND, LED1.cathode, LED2.cathode, J1.gnd, Q1.E, LCD1.VSS
  N7: LED1.anode, R1.Pin_0
  N8: LED2.anode, R2.Pin_0
